# Fritzing sketch Prototyp (saved by Fritzing 0.9.5d)
breadboards: 1

parts:
  Raspberry_Pi_1 = Raspberry Pi 3 [part_number=RPI-3-V1.2]
  DHT1 = DHT22 Humidity and Temperature Sensor

nets:
  3V3: Raspberry_Pi_1.3v3, DHT1.VDD
  N1: Raspberry_Pi_1.GIPO4, DHT1.DATA
  GND: Raspberry_Pi_1.GND, DHT1.GND
